# Fritzing sketch Smart Alarm (saved by Fritzing 1.0.4)
breadboards: 1

parts:
  J1 = STM32 Nucleo boards
  OLED_I2C1 = OLED 128x64 I2C Monochrome Display
  A1 = Wemos S2 Mini [part_number="WeMos D1 Mini Lite"]
  Keypad4x2 = Keypad Membran 4x4
  Reed_Switch = SWITCH-MOMENTARY-2 [package=reed_switch_pth]
  J2 = Piezo Speaker
  10K = Resistor [tolerance=±5% power=0.25W resistance=220 package=THT]
  Componente1 = RFID-RC522-v2
  PIR1 = PIR sensor
  10K_2 = Resistor [tolerance=±5% power=0.25W resistance=220 package=THT]
  10K_3 = Resistor [tolerance=±5% power=0.25W resistance=220 package=THT]

nets:
  N1: J1.PC6, Keypad4x2.Pin5
  N2: J1.PC5, Keypad4x2.Pin8
  N3: J1.PC11, Componente1.MISO
  N4: J1.PD2, Componente1.SDA
  N5: J1.D2, J2.pin2
  N6: J1.D4, A1.Pin_1, A1.Pin_9
  N7: J1.D7, Reed_Switch.2, 10K.Pin_1
  3V3: J1.3V3, Componente1.3.3V
  5V: J1.5V, A1.Pin_17, A1.Pin_25, PIR1.VDD
  N8: J1.PB2, Keypad4x2.Pin3
  N9: J1.PB1, Keypad4x2.Pin2
  N10: J1.PB15, Keypad4x2.Pin1
  N11: J1.PC4, Keypad4x2.Pin7
  N12: J1.PB8, A1.Pin_24, A1.Pin_32, 10K_2.Pin_0
  N13: J1.PB9, OLED_I2C1.SDA, A1.Pin_23, A1.Pin_31, 10K_3.Pin_0
  N14: J1.PC7, Keypad4x2.Pin6
  N15: J1.PB10, Keypad4x2.Pin4
  N16: J1.PC10, Componente1.SCK
  N17: J1.PC12, Componente1.MOSI
  N18: J1.PA15, Componente1.RST
  GND: J1.GND, OLED_I2C1.GND, A1.Pin_18, A1.Pin_26, Reed_Switch.1, J2.pin1, Componente1.GND, PIR1.GND
  N19: J1.PB7, PIR1.SIG
  N20: OLED_I2C1.VDD, 10K.Pin_0, 10K_2.Pin_1, 10K_3.Pin_1
  N21: A1.Pin_2, A1.Pin_10
  N22: A1.Pin_3, A1.Pin_11
  N23: A1.Pin_4, A1.Pin_12
  N24: A1.Pin_5, A1.Pin_13
  N25: A1.Pin_6, A1.Pin_14
  N26: A1.Pin_7, A1.Pin_15
  N27: A1.Pin_8, A1.Pin_16
  N28: A1.Pin_19, A1.Pin_27
  N29: A1.Pin_20, A1.Pin_28
  N30: A1.Pin_21, A1.Pin_29
  N31: A1.Pin_22, A1.Pin_30

custom parts:
  Wemos S2 Mini: A mini wifi board based on the ESP32-S2FN4R2.
  Keypad Membran 4x4: Membrane Keypad 4x4 Matrix
  RFID-RC522-v2: A simple China made RFID-RC522 Reader; do check the pin labels, as this is a MFRC522 based clone.
